# Fritzing sketch RemECG (saved by Fritzing 0.9.3b)
circuit board: 9.91006cm x 8.43736cm

parts:
  AD8232 = AD8232 HeartRate Monitor [part_number=SEN-12650 chip_label=IC package="DIP (Dual Inline) [THT]"]
  NodeMCU_v2 = NodeMCU V1.0
  SD_Card_Module = MicroSD Card Module
  SW = female pin header, 2 pins [form="♀ (female)"]
  5V = female pin header, 2 pins [form="♀ (female)"]
  Arduino_Nano_R3 = Arduino Nano (Rev3.0)

nets:
  GND: AD8232.GND, NodeMCU_v2.GND, SD_Card_Module.GND, 5V.pin2, Arduino_Nano_R3.GND
  3.3V: AD8232.3.3v, Arduino_Nano_R3.3V3
  N1: AD8232.OUTPUT, Arduino_Nano_R3.A0
  N2: AD8232.LO-, Arduino_Nano_R3.D3
  N3: AD8232.LO+, Arduino_Nano_R3.D2
  3V3: NodeMCU_v2.3V3, SD_Card_Module.VCC
  N4: NodeMCU_v2.D5, SD_Card_Module.SCK
  N5: NodeMCU_v2.D6, SD_Card_Module.MISO
  N6: NodeMCU_v2.D7, SD_Card_Module.MOSI
  N7: NodeMCU_v2.D8, SD_Card_Module.CS
  N8: NodeMCU_v2.RX, Arduino_Nano_R3.D1/TX
  N9: NodeMCU_v2.TX, Arduino_Nano_R3.D0/RX
  N10: NodeMCU_v2.Vin, SW.pin1
  N11: SW.pin2, 5V.pin1, Arduino_Nano_R3.5V

notes:
  +
  -
  RemECG

custom parts:
  AD8232 HeartRate Monitor: A DIP stand-in part for whatever IC you want. With 10 pins on a 600mil dual inline package (DIP) footprint.
  NodeMCU V1.0: ESP8266 based NodeMCU
